// Digital circuit Abs_Val.dig as structural Verilog
module Abs_Val (
  input  [7:0] INP,
  output [7:0] OUT
);

  wire [7:0] add_1_s, not_1_out;

  assign not_1_out = ~INP;  // Not not_1, 8 bits wide
  Add add_1 (.a(not_1_out[0]), .b(1'b0), .c_i(1'b1), .s(add_1_s[0]));  // open: c_o
  Multiplexer #(.Bits(8)) multiplexer_1 (.sel(INP[7]), .in_0(INP), .in_1(add_1_s), .out(OUT));
  // Pins of 1 and 8 bits meet at add_1_s
  // Pins of 1 and 8 bits meet at not_1_out
  // Pins of 1 and 8 bits meet at {8{1'b0}}
endmodule
