// Digital circuit Divider.dig as structural Verilog
module Divider (
  input  [15:0] INP_A,
  input  [15:0] INP_B,
  output [7:0] QUOTIENT,
  output [7:0] REM,
  output UNDEF
);

  wire xor_1_out;
  wire [0:0] multiplexer_1_out, multiplexer_1_out_2, multiplexer_1_out_3, multiplexer_1_out_4,
       multiplexer_1_out_5, multiplexer_1_out_6;
  wire [7:0] multiplexer_2_out, neg_1_out, neg_2_out, neg_3_out, step_rem_compare_1_compare,
       step_rem_compare_1_rem, step_rem_compare_3_rem, step_rem_compare_4_rem, step_rem_compare_5_rem,
       step_rem_compare_6_rem, step_rem_compare_7_rem, step_rem_compare_8_rem;
  wire [7:6] multiplexer_1_out_7;

  Neg #(.Bits(8)) neg_1 (.in(INP_A[7:0]), .out(neg_1_out));
  Multiplexer #(.Bits(8)) multiplexer_1 (
    .sel(INP_A[7]), .in_0(INP_A[7:0]), .in_1(neg_1_out),
    .out({multiplexer_1_out_7, multiplexer_1_out_6[0], multiplexer_1_out_5[0], multiplexer_1_out_4[0], multiplexer_1_out_3[0], multiplexer_1_out_2[0], multiplexer_1_out[0]}));
  Neg #(.Bits(8)) neg_2 (.in(INP_B[7:0]), .out(neg_2_out));
  Multiplexer #(.Bits(8)) multiplexer_2 (.sel(INP_B[7]), .in_0(INP_B[7:0]), .in_1(neg_2_out), .out(multiplexer_2_out));
  Step_rem_compare step_rem_compare_1 (
    .INP_A({{7{1'b0}}, multiplexer_1_out_7[7]}), .INP_B(multiplexer_2_out),
    .COMPARE(step_rem_compare_1_compare[7]), .REM(step_rem_compare_1_rem));
  Step_rem_compare step_rem_compare_2 (
    .INP_A({step_rem_compare_4_rem[6:0], multiplexer_1_out[0]}), .INP_B(multiplexer_2_out),
    .COMPARE(step_rem_compare_1_compare[0]), .REM(REM));
  Step_rem_compare step_rem_compare_3 (
    .INP_A({step_rem_compare_1_rem[6:0], multiplexer_1_out_7[6]}), .INP_B(multiplexer_2_out),
    .COMPARE(step_rem_compare_1_compare[6]), .REM(step_rem_compare_3_rem));
  Step_rem_compare step_rem_compare_4 (
    .INP_A({step_rem_compare_6_rem[6:0], multiplexer_1_out_2[0]}), .INP_B(multiplexer_2_out),
    .COMPARE(step_rem_compare_1_compare[1]), .REM(step_rem_compare_4_rem));
  Step_rem_compare step_rem_compare_5 (
    .INP_A({step_rem_compare_3_rem[6:0], multiplexer_1_out_6[0]}), .INP_B(multiplexer_2_out),
    .COMPARE(step_rem_compare_1_compare[5]), .REM(step_rem_compare_5_rem));
  Step_rem_compare step_rem_compare_6 (
    .INP_A({step_rem_compare_8_rem[6:0], multiplexer_1_out_3[0]}), .INP_B(multiplexer_2_out),
    .COMPARE(step_rem_compare_1_compare[2]), .REM(step_rem_compare_6_rem));
  Step_rem_compare step_rem_compare_7 (
    .INP_A({step_rem_compare_5_rem[6:0], multiplexer_1_out_5[0]}), .INP_B(multiplexer_2_out),
    .COMPARE(step_rem_compare_1_compare[4]), .REM(step_rem_compare_7_rem));
  Step_rem_compare step_rem_compare_8 (
    .INP_A({step_rem_compare_7_rem[6:0], multiplexer_1_out_4[0]}), .INP_B(multiplexer_2_out),
    .COMPARE(step_rem_compare_1_compare[3]), .REM(step_rem_compare_8_rem));
  xor xor_1 (xor_1_out, INP_A[7], INP_B[7]);
  Multiplexer #(.Bits(8)) multiplexer_3 (
    .sel(xor_1_out), .in_0(step_rem_compare_1_compare), .in_1(neg_3_out), .out(QUOTIENT));
  Neg #(.Bits(8)) neg_3 (.in(step_rem_compare_1_compare), .out(neg_3_out));
  nor nor_1 (UNDEF, INP_B[0], INP_B[1], INP_B[2], INP_B[3], INP_B[4], INP_B[5], INP_B[6], INP_B[7]);
endmodule
