// Digital circuit Multiplier.dig as structural Verilog
module Multiplier (
  input  [15:0] INP_A,
  input  [15:0] INP_B,
  output [15:0] OUT,
  output OUTBOUNDS,
  output Negative_Flag
);

  wire [7:0] add_1_s, and_1_out, and_2_out, and_3_out, and_4_out, and_5_out, and_6_out, and_7_out, and_8_out,
       multiplexer_1_out, multiplexer_2_out, multiplexer_3_out, multiplexer_4_out, multiplexer_5_out,
       multiplexer_6_out, multiplexer_7_out, multiplexer_8_out, multiplexer_9_out, multiplexer_10_out,
       neg_1_out, neg_2_out;
  wire [15:0] add_2_s, add_3_s, add_4_s, add_5_s, add_6_s, add_7_s, add_8_s, neg_3_out;

  Neg #(.Bits(8)) neg_1 (.in(INP_A[7:0]), .out(neg_1_out));
  Multiplexer #(.Bits(8)) multiplexer_1 (.sel(INP_A[7]), .in_0(INP_A[7:0]), .in_1(neg_1_out), .out(multiplexer_1_out));
  Multiplexer #(.Bits(8)) multiplexer_2 (
    .sel(multiplexer_1_out[0]), .in_0({8{1'b0}}), .in_1({8{1'b1}}), .out(multiplexer_2_out));
  Multiplexer #(.Bits(8)) multiplexer_3 (
    .sel(multiplexer_1_out[1]), .in_0({8{1'b0}}), .in_1({8{1'b1}}), .out(multiplexer_3_out));
  Multiplexer #(.Bits(8)) multiplexer_4 (
    .sel(multiplexer_1_out[2]), .in_0({8{1'b0}}), .in_1({8{1'b1}}), .out(multiplexer_4_out));
  Multiplexer #(.Bits(8)) multiplexer_5 (
    .sel(multiplexer_1_out[3]), .in_0({8{1'b0}}), .in_1({8{1'b1}}), .out(multiplexer_5_out));
  Multiplexer #(.Bits(8)) multiplexer_6 (
    .sel(multiplexer_1_out[4]), .in_0({8{1'b0}}), .in_1({8{1'b1}}), .out(multiplexer_6_out));
  Multiplexer #(.Bits(8)) multiplexer_7 (
    .sel(multiplexer_1_out[5]), .in_0({8{1'b0}}), .in_1({8{1'b1}}), .out(multiplexer_7_out));
  Multiplexer #(.Bits(8)) multiplexer_8 (
    .sel(multiplexer_1_out[6]), .in_0({8{1'b0}}), .in_1({8{1'b1}}), .out(multiplexer_8_out));
  Multiplexer #(.Bits(8)) multiplexer_9 (
    .sel(multiplexer_1_out[7]), .in_0({8{1'b0}}), .in_1({8{1'b1}}), .out(multiplexer_9_out));
  Neg #(.Bits(8)) neg_2 (.in(INP_B[7:0]), .out(neg_2_out));
  Multiplexer #(.Bits(8)) multiplexer_10 (
    .sel(INP_B[7]), .in_0(INP_B[7:0]), .in_1(neg_2_out), .out(multiplexer_10_out));
  assign and_1_out = multiplexer_2_out & multiplexer_10_out;  // And and_1, 8 bits wide
  assign and_2_out = multiplexer_3_out & multiplexer_10_out;  // And and_2, 8 bits wide
  assign and_3_out = multiplexer_4_out & multiplexer_10_out;  // And and_3, 8 bits wide
  assign and_4_out = multiplexer_5_out & multiplexer_10_out;  // And and_4, 8 bits wide
  assign and_5_out = multiplexer_6_out & multiplexer_10_out;  // And and_5, 8 bits wide
  assign and_6_out = multiplexer_7_out & multiplexer_10_out;  // And and_6, 8 bits wide
  assign and_7_out = multiplexer_8_out & multiplexer_10_out;  // And and_7, 8 bits wide
  assign and_8_out = multiplexer_9_out & multiplexer_10_out;  // And and_8, 8 bits wide
  Add #(.Bits(8)) add_1 (.a(INP_B[15:8]), .b(INP_A[15:8]), .c_i(1'b0), .s(add_1_s));  // open: c_o
  Add #(.Bits(16)) add_2 (
    .a({{8{1'b0}}, and_1_out}), .b({{7{1'b0}}, and_2_out, 1'b0}), .c_i(1'b0), .s(add_2_s));  // open: c_o
  Add #(.Bits(16)) add_3 (
    .a({{6{1'b0}}, and_3_out, 2'b00}), .b({{5{1'b0}}, and_4_out, 3'b000}), .c_i(1'b0), .s(add_3_s));  // open: c_o
  Add #(.Bits(16)) add_4 (
    .a({4'b0000, and_5_out, 4'b0000}), .b({3'b000, and_6_out, {5{1'b0}}}), .c_i(1'b0), .s(add_4_s));  // open: c_o
  Add #(.Bits(16)) add_5 (
    .a({2'b00, and_7_out, {6{1'b0}}}), .b({1'b0, and_8_out, {7{1'b0}}}), .c_i(1'b0), .s(add_5_s));  // open: c_o
  or or_1 (OUTBOUNDS, add_1_s[0], add_1_s[1], add_1_s[2], add_1_s[3], add_1_s[4], add_1_s[5], add_1_s[6], add_1_s[7]);
  xor xor_1 (Negative_Flag, INP_B[7], INP_A[7]);
  Add #(.Bits(16)) add_6 (.a(add_2_s), .b(add_3_s), .c_i(1'b0), .s(add_6_s));  // open: c_o
  Add #(.Bits(16)) add_7 (.a(add_4_s), .b(add_5_s), .c_i(1'b0), .s(add_7_s));  // open: c_o
  Add #(.Bits(16)) add_8 (.a(add_6_s), .b(add_7_s), .c_i(1'b0), .s(add_8_s));  // open: c_o
  Multiplexer #(.Bits(16)) multiplexer_11 (.sel(Negative_Flag), .in_0(add_8_s), .in_1(neg_3_out), .out(OUT));
  Neg #(.Bits(16)) neg_3 (.in(add_8_s), .out(neg_3_out));
endmodule
