// Digital circuit Step_rem_compare.dig as structural Verilog
module Step_rem_compare (
  input  [7:0] INP_A,
  input  [7:0] INP_B,
  output COMPARE,
  output [7:0] REM
);

  wire [7:0] add_1_s, not_1_out;

  assign not_1_out = ~INP_B;  // Not not_1, 8 bits wide
  Add #(.Bits(8)) add_1 (.a(INP_A), .b(not_1_out), .c_i(1'b1), .s(add_1_s));  // open: c_o
  not not_2 (COMPARE, add_1_s[7]);
  Multiplexer #(.Bits(8)) multiplexer_1 (.sel(add_1_s[7]), .in_0(add_1_s), .in_1(INP_A), .out(REM));
endmodule
