// Digital circuit basic-control-unit.dig as structural Verilog
module basic_control_unit (
  input  [15:0] INST,
  input  Z_FLAG,
  output [1:0] ALUOP,
  output [1:0] DMUX,
  output STR,
  output LDR,
  output FLEN,
  output EXEC,
  output SETH,
  output [2:0] RS1,
  output [2:0] RS2,
  output [2:0] WS,
  output WE
);

  wire multiplexer_5_out, nand_1_out, not_1_out, not_2_out, not_3_out;
  wire [1:0] decoder_1_out_0, multiplexer_1_out, multiplexer_3_out;

  not not_1 (not_1_out, Z_FLAG);
  Multiplexer #(.Bits(2)) multiplexer_1 (.sel(INST[12]), .in_0(2'b11), .in_1(2'b01), .out(multiplexer_1_out));
  Multiplexer #(.Selector_Bits(2), .Bits(2)) multiplexer_2 (
    .sel(INST[15:14]), .in_0(2'b10), .in_1(multiplexer_1_out), .in_2(2'b00), .in_3(2'b11), .out(DMUX));
  Decoder decoder_1 (.sel(INST[12]), .out_0(decoder_1_out_0[0]), .out_1(decoder_1_out_0[1]));
  not not_2 (not_2_out, INST[14]);
  // And and_1 has open pins: In_1=not_2_out, In_2=INST[15], out=open
  Multiplexer #(.Bits(2)) multiplexer_3 (.sel(INST[14]), .in_0(2'b00), .in_1(decoder_1_out_0), .out(multiplexer_3_out));
  nand nand_1 (nand_1_out, DMUX[0], DMUX[1]);
  nand nand_2 (EXEC, INST[11], not_1_out);
  Multiplexer #(.Bits(3)) multiplexer_4 (.sel(multiplexer_3_out[0]), .in_0(INST[2:0]), .in_1(INST[10:8]), .out(RS2));
  and and_2 (WE, nand_1_out, EXEC);
  and and_3 (LDR, multiplexer_3_out[1], EXEC);
  and and_4 (FLEN, INST[15], EXEC);
  not not_3 (not_3_out, INST[12]);
  Multiplexer #(.Selector_Bits(2)) multiplexer_5 (
    .sel(INST[15:14]), .in_0(1'b0), .in_1(not_3_out), .in_2(1'b0), .in_3(1'b0), .out(multiplexer_5_out));
  and and_5 (STR, multiplexer_5_out, EXEC);

  assign ALUOP = INST[13:12];
  assign RS1 = INST[6:4];
  assign SETH = INST[12];
  assign WS = INST[10:8];

  // Notes on the sheet:
  //   Z
  //   Rd
  //   Ra
  //   Rb
  //   opcode
endmodule

/* Test case All Tests:
	INST                                    WE  ALUOP  RS1   RS2  WS  STR  LDR DMUX

let aluop  = 0b1000;
let ldrop  = 0b0101;
let strop  = 0b0100;
let movlop = 0b0000;

loop(rd, 1<<3)
loop(ra, 1<<3)
loop(rb, 1<<3)

loop(i, 4)
	((aluop+i)<<12 | rd<<8 | ra<<4 | rb<<0) 1  (i)     (ra)  (rb) (rd)  0   X    0  #test add/sub/and/xor
end loop

	(ldrop    <<12 | rd<<8 | ra<<4 )        1  X       (ra)  x    (rd)  0   1    1  #test ldr
	(strop    <<12 | rd<<8 | ra<<4 )        0  X       (ra)  (rd)  X    1   X    X  #test str
	
	let imm = random(256);
	(movlop   <<12 | rd<<8 | imm )          1  X       X      X   (rd)  0   X    2  #test movl

end loop
end loop
end loop
*/

/* Test case WS:
	INST                                    WS 

let aluop  = 0b1000;
let ldrop  = 0b0101;
let strop  = 0b0100;
let movlop = 0b0000;

loop(rd, 1<<3)
loop(ra, 1<<3)
loop(rb, 1<<3)

loop(i, 4)
	((aluop+i)<<12 | rd<<8 | ra<<4 | rb<<0) (rd)  #test add/sub/and/xor
end loop

	(ldrop    <<12 | rd<<8 | ra<<4 )        (rd)   #test ldr
	(strop    <<12 | rd<<8 | ra<<4 )        X     #test str
	
	let imm = random(256);
	(movlop   <<12 | rd<<8 | imm )          (rd)  #test movl

end loop
end loop
end loop
*/

/* Test case RS1:
	INST                                    RS1  

let aluop  = 0b1000;
let ldrop  = 0b0101;
let strop  = 0b0100;
let movlop = 0b0000;

loop(rd, 1<<3)
loop(ra, 1<<3)
loop(rb, 1<<3)

loop(i, 4)
	((aluop+i)<<12 | rd<<8 | ra<<4 | rb<<0) (ra)  #test add/sub/and/xor
end loop

	(ldrop    <<12 | rd<<8 | ra<<4 )        (ra)  #test ldr
	(strop    <<12 | rd<<8 | ra<<4 )        (ra)  #test str

end loop
end loop
end loop
*/

/* Test case RS2:
	INST                                    RS2  

let aluop  = 0b1000;
let ldrop  = 0b0101;
let strop  = 0b0100;
let movlop = 0b0000;

loop(rd, 1<<3)
loop(ra, 1<<3)
loop(rb, 1<<3)

loop(i, 4)
	((aluop+i)<<12 | rd<<8 | ra<<4 | rb<<0) (rb) #test add/sub/and/xor
end loop
	(strop    <<12 | rd<<8 | ra<<4 )        (rd) #test str

end loop
end loop
end loop
*/

/* Test case STR:
	INST                                    STR 

let aluop  = 0b1000;
let ldrop  = 0b0101;
let strop  = 0b0100;
let movlop = 0b0000;

loop(rd, 1<<3)
loop(ra, 1<<3)
loop(rb, 1<<3)

loop(i, 4)
	((aluop+i)<<12 | rd<<8 | ra<<4 | rb<<0) 0  #test add/sub/and/xor
end loop

	(ldrop    <<12 | rd<<8 | ra<<4 )        0  #test ldr
	(strop    <<12 | rd<<8 | ra<<4 )        1  #test str
	
	let imm = random(256);
	(movlop   <<12 | rd<<8 | imm )          0  #test movl

end loop
end loop
end loop
*/

/* Test case WE:
	INST                                    WE  

let aluop  = 0b1000;
let ldrop  = 0b0101;
let strop  = 0b0100;
let movlop = 0b0000;

loop(rd, 1<<3)
loop(ra, 1<<3)
loop(rb, 1<<3)

loop(i, 4)
	((aluop+i)<<12 | rd<<8 | ra<<4 | rb<<0) 1  #test add/sub/and/xor
end loop

	(ldrop    <<12 | rd<<8 | ra<<4 )        1  #test ldr
	(strop    <<12 | rd<<8 | ra<<4 )        0  #test str
	
	let imm = random(256);
	(movlop   <<12 | rd<<8 | imm )          1  #test movl

end loop
end loop
end loop
*/

/* Test case LDR:
	INST                                    LDR 

let aluop  = 0b1000;
let ldrop  = 0b0101;
let strop  = 0b0100;
let movlop = 0b0000;

loop(rd, 1<<3)
loop(ra, 1<<3)
loop(rb, 1<<3)

loop(i, 4)
	((aluop+i)<<12 | rd<<8 | ra<<4 | rb<<0) X    #test add/sub/and/xor
end loop

	(ldrop    <<12 | rd<<8 | ra<<4 )        1    #test ldr
	(strop    <<12 | rd<<8 | ra<<4 )        X    #test str
	
	let imm = random(256);
	(movlop   <<12 | rd<<8 | imm )          X    #test movl

end loop
end loop
end loop
*/

/* Test case DMUX:
	INST                                    DMUX

let aluop  = 0b1000;
let ldrop  = 0b0101;
let strop  = 0b0100;
let movlop = 0b0000;

loop(rd, 1<<3)
loop(ra, 1<<3)
loop(rb, 1<<3)

loop(i, 4)
	((aluop+i)<<12 | rd<<8 | ra<<4 | rb<<0) 0  #test add/sub/and/xor
end loop

	(ldrop    <<12 | rd<<8 | ra<<4 )        1  #test ldr
	
	let imm = random(256);
	(movlop   <<12 | rd<<8 | imm )          2  #test movl

end loop
end loop
end loop
*/

/* Test case ALUOP:
	INST                                    ALUOP 

let aluop  = 0b1000;
let ldrop  = 0b0101;
let strop  = 0b0100;
let movlop = 0b0000;

loop(rd, 1<<3)
loop(ra, 1<<3)
loop(rb, 1<<3)

loop(i, 4)
	((aluop+i)<<12 | rd<<8 | ra<<4 | rb<<0) (i)    #test add/sub/and/xor
end loop

end loop
end loop
end loop
*/
