// Digital circuit reg_file.dig as structural Verilog
module reg_file (
  input  [2:0] RS1,
  input  [2:0] RS2,
  input  [2:0] WS,
  input  WE,
  input  [15:0] IN,
  input  clk,
  output [15:0] OUT1,
  output [15:0] OUT2,
  output [15:0] OUT3
);

  wire and_1_out, and_2_out, and_3_out, and_4_out, and_5_out, decoder_1_out_0, decoder_1_out_1,
       decoder_1_out_2, decoder_1_out_3, decoder_1_out_4;
  wire [15:0] demultiplexer_1_out_1, demultiplexer_1_out_2, demultiplexer_1_out_3, demultiplexer_1_out_4,
       R1_q, R2_q, R3_q, R4_q;

  Decoder #(.Selector_Bits(3)) decoder_1 (
    .sel(WS), .out_0(decoder_1_out_0), .out_1(decoder_1_out_1), .out_2(decoder_1_out_2),
    .out_3(decoder_1_out_3), .out_4(decoder_1_out_4));  // open: out_5, out_6, out_7
  Demultiplexer #(.Selector_Bits(3), .Bits(16)) demultiplexer_1 (
    .sel(WS), .in(IN), .out_1(demultiplexer_1_out_1), .out_2(demultiplexer_1_out_2),
    .out_3(demultiplexer_1_out_3), .out_4(demultiplexer_1_out_4));  // open: out_0, out_5, out_6, out_7
  and and_1 (and_1_out, WE, decoder_1_out_0);
  and and_2 (and_2_out, WE, decoder_1_out_1);
  and and_3 (and_3_out, WE, decoder_1_out_2);
  and and_4 (and_4_out, WE, decoder_1_out_3);
  and and_5 (and_5_out, WE, decoder_1_out_4);
  Register #(.Bits(16)) R0 (.D({16{1'b0}}), .C(clk), .en(and_1_out));  // open: Q
  Register #(.Bits(16)) R1 (.D(demultiplexer_1_out_1), .C(clk), .en(and_2_out), .Q(R1_q));
  Register #(.Bits(16)) R2 (.D(demultiplexer_1_out_2), .C(clk), .en(and_3_out), .Q(R2_q));
  Register #(.Bits(16)) R3 (.D(demultiplexer_1_out_3), .C(clk), .en(and_4_out), .Q(R3_q));
  Register #(.Bits(16)) R4 (.D(demultiplexer_1_out_4), .C(clk), .en(and_5_out), .Q(R4_q));
  Multiplexer #(.Selector_Bits(3), .Bits(16)) multiplexer_1 (
    .sel(RS2), .in_0({16{1'b0}}), .in_1(R1_q), .in_2(R2_q), .in_3(R3_q), .in_4(R4_q), .in_5({16{1'b0}}),
    .in_6({16{1'b0}}), .in_7({16{1'b0}}), .out(OUT2));
  Multiplexer #(.Selector_Bits(3), .Bits(16)) multiplexer_2 (
    .sel(RS1), .in_0({16{1'b0}}), .in_1(R1_q), .in_2(R2_q), .in_3(R3_q), .in_4(R4_q), .in_5({16{1'b0}}),
    .in_6({16{1'b0}}), .in_7({16{1'b0}}), .out(OUT1));
  Multiplexer #(.Selector_Bits(3), .Bits(16)) multiplexer_3 (
    .sel(WS), .in_0({16{1'b0}}), .in_1(R1_q), .in_2(R2_q), .in_3(R3_q), .in_4(R4_q), .in_5({16{1'b0}}),
    .in_6({16{1'b0}}), .in_7({16{1'b0}}), .out(OUT3));

  // Notes on the sheet:
  //   RS1: The index of the register which should output its value to OUT1.
  //   RS2: The index of the register which should output its value to OUT2.
  //   WS: The index of the register which should save the value on IN on the next clock cycle (if WE is high).
  //   WE: Whether the register selected by WS should save the value from IN on the next cycle.
  //   IN: The value to be saved into the register specified by WS if WE is high,
  //   OUT1: The value in the register specified by RS1.
  //   OUT2: The value in the register specified by RS2.
  //   OUT3: The value in the register specified by RS2.
endmodule

/* Test case:
clk RS1 RS2 WS WE IN OUT1 OUT2
c 0 0 0 1 0x1234 0x0000 0x0000
c 1 0 1 1 0xBEEF 0xBEEF 0x0000
c 2 1 2 1 0xDEAD 0xDEAD 0xBEEF
c 3 2 3 1 0xFFFF 0xFFFF 0xDEAD
c 3 2 3 0 0xABCD 0xFFFF 0xDEAD
c 3 2 2 0 0xABCD 0xFFFF 0xDEAD
c 1 0 1 0 0xABCD 0xBEEF 0x0000
c 1 0 0 0 0xABCD 0xBEEF 0x0000
c 1 0 2 1 0xBADE 0xBEEF 0x0000
c 0 2 2 1 0xBADE 0x0000 0xBADE
c 0 0 2 0 0x1234 0x0000 0x0000
c 2 3 0 1 0x0000 0xBADE 0xFFFF
c 0 0 2 0 0x1234 0x0000 0x0000
*/
